// Logisim project college-kid-lunch.circ as structural Verilog: 1 circuit, main circuit main
module main (
  input  Temp,
  input  Spicy,
  output Salad,
  output Sushi,
  output Burrito,
  output Ramen
);

  wire not_1_out, not_2_out;

  not not_1 (not_1_out, Temp);
  not not_2 (not_2_out, Spicy);
  and CM (Salad, Temp, Spicy);
  and CH (Sushi, Temp, Temp, not_2_out, not_2_out);
  and HM (Burrito, not_1_out, Spicy);
  and HS (Ramen, not_1_out, not_2_out);

  // Notes on the sheet:
  //   Poor College Kid Lunch
endmodule
