// Logisim project Homework3Problem13.circ as structural Verilog: 1 circuit, main circuit main
module main (
  input  A,
  input  B,
  input  C,
  input  D,
  input  A_2,
  input  B_2,
  input  C_2,
  input  D_2,
  output out_9,
  output out_10
);

  wire A_prime_B_out, A_prime_B_prime_out, A_xor_B_2_out, A_xor_B__prime_2_out, A_xor_B__prime_out,
       A_xor_B_out, AB_out, AB_prime_out, C_prime_D_out, C_prime_D_prime_out, C_xor_D_2_out, C_xor_D_out,
       CD_out, CD_prime_out, nand_1_out, nand_2_out, nand_3_out, nand_4_out, nand_5_out, nor_1_out,
       nor_2_out, nor_3_out, nor_4_out, nor_5_out, nor_6_out;

  nand nand_1 (nand_1_out, A, A);
  nor nor_1 (nor_1_out, A_2, A_2);
  nand nand_2 (nand_2_out, B, B);
  nor nor_2 (nor_2_out, B_2, B_2);
  nand nand_3 (nand_3_out, C, C);
  nor nor_3 (nor_3_out, C_2, C_2);
  nand nand_4 (nand_4_out, D, D);
  nor nor_4 (nor_4_out, D_2, D_2);
  nand AB_prime (AB_prime_out, A, nand_2_out);
  nand A_prime_B (A_prime_B_out, B, nand_1_out);
  nand CD_prime (CD_prime_out, C, nand_4_out);
  nand C_prime_D (C_prime_D_out, nand_3_out, D);
  nor AB (AB_out, A_2, B_2);
  nor A_prime_B_prime (A_prime_B_prime_out, nor_2_out, nor_1_out);
  nor CD (CD_out, C_2, D_2);
  nor C_prime_D_prime (C_prime_D_prime_out, nor_3_out, nor_4_out);
  nand A_xor_B (A_xor_B_out, AB_prime_out, A_prime_B_out);
  nand C_xor_D (C_xor_D_out, CD_prime_out, C_prime_D_out);
  nor A_xor_B_2 (A_xor_B_2_out, AB_out, A_prime_B_prime_out);
  nor C_xor_D_2 (C_xor_D_2_out, CD_out, C_prime_D_prime_out);
  not A_xor_B__prime (A_xor_B__prime_out, A_xor_B_out);  // NAND_Gate
  not A_xor_B__prime_2 (A_xor_B__prime_2_out, A_xor_B_2_out);  // NOR_Gate
  nand nand_5 (nand_5_out, A_xor_B__prime_out, C_xor_D_out);
  not nor_5 (nor_5_out, A_xor_B__prime_2_out);  // NOR_Gate
  not nor_6 (nor_6_out, C_xor_D_2_out);  // NOR_Gate
  not nand_6 (out_9, nand_5_out);  // NAND_Gate
  nor nor_7 (out_10, nor_5_out, nor_6_out);
endmodule
