// Logisim project Lab1_Part2_3_Perez.circ as structural Verilog: 1 circuit, main circuit main
module main (
  input  x,
  input  y,
  output xy__prime,
  output xy__prime_2,
  output x___y__prime,
  output x___y__prime_2
);

  wire AND_out, OR_out;

  nand NAND (xy__prime, x, y);
  and AND (AND_out, x, y);
  not not_1 (xy__prime_2, AND_out);
  nor NOR (x___y__prime, x, y);
  or OR (OR_out, x, y);
  not not_2 (x___y__prime_2, OR_out);
endmodule
