// Logisim project Lab1_Part4_Perez.circ as structural Verilog: 1 circuit, main circuit main
module main (
  input  IsWeekend,
  input  IsSunny,
  output Hiking,
  output Home,
  output Tennis,
  output Rocketball
);

  wire not_1_out;

  not not_1 (not_1_out, IsSunny);
  and and_1 (Hiking, IsWeekend, IsSunny);
  nor nor_1 (Home, IsWeekend, IsSunny);
  and and_2 (Tennis, IsWeekend, not_1_out);
  nor nor_2 (Rocketball, IsWeekend, not_1_out);

  // Notes on the sheet:
  //   Brandon Perez - Part 4 Lab 1
endmodule
