// Logisim project Lab2_Part1_2_3_Perez.circ as structural Verilog: 1 circuit, main circuit main
module main (
  input  x,
  input  y,
  input  z,
  output Left_Hand,
  output Right_Hand,
  output Left_Hand_2,
  output Right_Hand_2,
  output out_8,
  output out_9,
  output x_prime___y_prime____xy,
  output x_prime_y_prime__x_y
);

  wire and_2_out, and_3_out, and_4_out, and_6_out, and_7_out, and_8_out, not_3_out, not_4_out, or_1_out,
       or_4_out, or_5_out, or_6_out, or_7_out, or_8_out;

  and and_1 (Left_Hand, x, or_1_out);
  or or_1 (or_1_out, y, z);
  and and_2 (and_2_out, x, y);
  or or_2 (Right_Hand, and_2_out, and_3_out);
  and and_3 (and_3_out, x, z);
  or or_3 (Left_Hand_2, x, and_4_out);
  and and_4 (and_4_out, y, z);
  or or_4 (or_4_out, x, y);
  and and_5 (Right_Hand_2, or_4_out, or_5_out);
  or or_5 (or_5_out, x, z);
  not not_1 (out_8, or_6_out);
  or or_6 (or_6_out, x, y, z);
  not not_2 (out_9, and_6_out);
  and and_6 (and_6_out, x, y, z);
  or or_7 (or_7_out, x, y);
  not not_3 (not_3_out, or_7_out);
  and and_7 (and_7_out, x, y);
  not not_4 (not_4_out, and_8_out);
  and and_8 (and_8_out, x, y);
  or or_8 (or_8_out, x, y);
  or or_9 (x_prime___y_prime____xy, not_3_out, and_7_out);
  and and_9 (x_prime_y_prime__x_y, not_4_out, or_8_out);

  // Notes on the sheet:
  //   Part 3
  //   Part 2, Problem 1
  //   Part 2, Problem 2
  //   Part 1, Problem 1
  //   Part 1, Problem 2
endmodule
