// Logisim project Lab3Part1.circ as structural Verilog: 1 circuit, main circuit main
module main (
  input  [15:0] W,
  input  [15:0] X,
  input  [15:0] Y,
  input  [15:0] Z,
  input  [15:0] W_2,
  input  [15:0] X_2,
  input  [15:0] Y_2,
  input  [15:0] Z_2,
  output [15:0] out_9,
  output [15:0] out_10
);

  wire [15:0] nand_1_out, nand_2_out, nand_3_out, nand_4_out, not_1_out, not_2_out, not_3_out, not_4_out,
       or_1_out, or_2_out, w_prime_out, w_prime_x_prime_y_prime_2_out, w_prime_x_prime_y_prime_out,
       w_prime_x_prime_z_prime_2_out, w_prime_x_prime_z_prime_out, w_prime_y_prime_z_prime_2_out,
       w_prime_y_prime_z_prime_out, wxy_2_out, wxy_out, wxz_2_out, wxz_out, wyz_2_out, wyz_out, x_prime_out,
       x_prime_y_prime_z_prime_2_out, x_prime_y_prime_z_prime_out, xyz_2_out, xyz_out, y_prime_out,
       z_prime_out;

  assign w_prime_out = ~(W & W);  // NAND_Gate w_prime, 16 bits wide
  assign x_prime_out = ~(X & X);  // NAND_Gate x_prime, 16 bits wide
  assign y_prime_out = ~(Y & Y);  // NAND_Gate y_prime, 16 bits wide
  assign z_prime_out = ~(Z & Z);  // NAND_Gate z_prime, 16 bits wide
  assign wxy_out = ~(W & X & Y);  // NAND_Gate wxy, 16 bits wide
  assign wxz_out = ~(W & X & Z);  // NAND_Gate wxz, 16 bits wide
  assign wyz_out = ~(W & Y & Z);  // NAND_Gate wyz, 16 bits wide
  assign xyz_out = ~(X & Y & Z);  // NAND_Gate xyz, 16 bits wide
  assign w_prime_x_prime_y_prime_out = ~(w_prime_out & x_prime_out & y_prime_out);  // NAND_Gate w_prime_x_prime_y_prime, 16 bits wide
  assign w_prime_x_prime_z_prime_out = ~(w_prime_out & x_prime_out & z_prime_out);  // NAND_Gate w_prime_x_prime_z_prime, 16 bits wide
  assign w_prime_y_prime_z_prime_out = ~(w_prime_out & y_prime_out & z_prime_out);  // NAND_Gate w_prime_y_prime_z_prime, 16 bits wide
  assign x_prime_y_prime_z_prime_out = ~(x_prime_out & y_prime_out & z_prime_out);  // NAND_Gate x_prime_y_prime_z_prime, 16 bits wide
  assign nand_1_out = ~(wxy_out & wxz_out & wyz_out & xyz_out);  // NAND_Gate nand_1, 16 bits wide
  assign nand_2_out = ~(w_prime_x_prime_y_prime_out & w_prime_x_prime_z_prime_out & w_prime_y_prime_z_prime_out & x_prime_y_prime_z_prime_out);  // NAND_Gate nand_2, 16 bits wide
  assign nand_3_out = ~(nand_1_out & nand_1_out);  // NAND_Gate nand_3, 16 bits wide
  assign nand_4_out = ~(nand_2_out & nand_2_out);  // NAND_Gate nand_4, 16 bits wide
  assign out_9 = ~(nand_3_out & nand_4_out);  // NAND_Gate nand_5, 16 bits wide
  assign not_1_out = ~W_2;  // NOT_Gate not_1, 16 bits wide
  assign not_2_out = ~X_2;  // NOT_Gate not_2, 16 bits wide
  assign not_3_out = ~Y_2;  // NOT_Gate not_3, 16 bits wide
  assign not_4_out = ~Z_2;  // NOT_Gate not_4, 16 bits wide
  assign wxy_2_out = W_2 & X_2 & Y_2;  // AND_Gate wxy_2, 16 bits wide
  assign wxz_2_out = W_2 & X_2 & Z_2;  // AND_Gate wxz_2, 16 bits wide
  assign wyz_2_out = W_2 & Y_2 & Z_2;  // AND_Gate wyz_2, 16 bits wide
  assign xyz_2_out = X_2 & Y_2 & Z_2;  // AND_Gate xyz_2, 16 bits wide
  assign w_prime_x_prime_y_prime_2_out = not_1_out & not_2_out & not_3_out;  // AND_Gate w_prime_x_prime_y_prime_2, 16 bits wide
  assign w_prime_x_prime_z_prime_2_out = not_1_out & not_2_out & not_4_out;  // AND_Gate w_prime_x_prime_z_prime_2, 16 bits wide
  assign w_prime_y_prime_z_prime_2_out = not_1_out & not_3_out & not_4_out;  // AND_Gate w_prime_y_prime_z_prime_2, 16 bits wide
  assign x_prime_y_prime_z_prime_2_out = not_2_out & not_3_out & not_4_out;  // AND_Gate x_prime_y_prime_z_prime_2, 16 bits wide
  assign or_1_out = wxy_2_out | wxz_2_out | wyz_2_out | xyz_2_out;  // OR_Gate or_1, 16 bits wide
  assign or_2_out = w_prime_x_prime_y_prime_2_out | w_prime_x_prime_z_prime_2_out | w_prime_y_prime_z_prime_2_out | x_prime_y_prime_z_prime_2_out;  // OR_Gate or_2, 16 bits wide
  assign out_10 = or_1_out | or_2_out;  // OR_Gate or_3, 16 bits wide

  // Notes on the sheet:
  //   Brandon Perez - Lab 3 Part 1
  //   Universal NAND Solution
  //   AND / OR / NOT Gates Solution
endmodule
