// Logisim project Lab3Part2.circ as structural Verilog: 1 circuit, main circuit main
module main (
  input  [15:0] W,
  input  [15:0] X,
  input  [15:0] Y,
  input  [15:0] Z,
  input  [15:0] W_2,
  input  [15:0] X_2,
  input  [15:0] Y_2,
  input  [15:0] Z_2,
  output [15:0] out_9,
  output [15:0] out_10
);

  wire [15:0] nand_1_out, nand_2_out, nand_3_out, nand_4_out, nand_5_out, nand_6_out, nand_7_out, nand_8_out,
       not_1_out, not_2_out, not_3_out, not_4_out, or_1_out, or_2_out, w_prime_x_prime_y_prime_z_2_out,
       w_prime_x_prime_y_prime_z_out, w_prime_x_prime_yz_prime_2_out, w_prime_x_prime_yz_prime_out,
       w_prime_xy_prime_z_prime_2_out, w_prime_xy_prime_z_prime_out, w_prime_xyz_2_out, w_prime_xyz_out,
       wx_prime_y_prime_z_prime_2_out, wx_prime_y_prime_z_prime_out, wx_prime_yz_2_out, wx_prime_yz_out,
       wxy_prime_z_2_out, wxy_prime_z_out, wxyz_prime_2_out, wxyz_prime_out;

  assign nand_1_out = ~(W & W);  // NAND_Gate nand_1, 16 bits wide
  assign nand_2_out = ~(X & X);  // NAND_Gate nand_2, 16 bits wide
  assign nand_3_out = ~(Y & Y);  // NAND_Gate nand_3, 16 bits wide
  assign nand_4_out = ~(Z & Z);  // NAND_Gate nand_4, 16 bits wide
  assign w_prime_x_prime_y_prime_z_out = ~(nand_1_out & nand_2_out & nand_3_out & Z);  // NAND_Gate w_prime_x_prime_y_prime_z, 16 bits wide
  assign w_prime_x_prime_yz_prime_out = ~(nand_1_out & nand_2_out & Y & nand_4_out);  // NAND_Gate w_prime_x_prime_yz_prime, 16 bits wide
  assign w_prime_xy_prime_z_prime_out = ~(nand_1_out & X & nand_3_out & nand_4_out);  // NAND_Gate w_prime_xy_prime_z_prime, 16 bits wide
  assign w_prime_xyz_out = ~(nand_1_out & X & Y & Z);  // NAND_Gate w_prime_xyz, 16 bits wide
  assign wxy_prime_z_out = ~(W & X & nand_3_out & Z);  // NAND_Gate wxy_prime_z, 16 bits wide
  assign wxyz_prime_out = ~(W & X & Y & nand_4_out);  // NAND_Gate wxyz_prime, 16 bits wide
  assign wx_prime_y_prime_z_prime_out = ~(W & nand_2_out & nand_3_out & nand_4_out);  // NAND_Gate wx_prime_y_prime_z_prime, 16 bits wide
  assign wx_prime_yz_out = ~(W & nand_2_out & Y & Z);  // NAND_Gate wx_prime_yz, 16 bits wide
  assign nand_5_out = ~(w_prime_x_prime_y_prime_z_out & w_prime_x_prime_yz_prime_out & w_prime_xy_prime_z_prime_out & w_prime_xyz_out);  // NAND_Gate nand_5, 16 bits wide
  assign nand_6_out = ~(wxy_prime_z_out & wxyz_prime_out & wx_prime_y_prime_z_prime_out & wx_prime_yz_out);  // NAND_Gate nand_6, 16 bits wide
  assign nand_7_out = ~(nand_5_out & nand_5_out);  // NAND_Gate nand_7, 16 bits wide
  assign nand_8_out = ~(nand_6_out & nand_6_out);  // NAND_Gate nand_8, 16 bits wide
  assign out_9 = ~(nand_7_out & nand_8_out);  // NAND_Gate nand_9, 16 bits wide
  assign not_1_out = ~W_2;  // NOT_Gate not_1, 16 bits wide
  assign not_2_out = ~X_2;  // NOT_Gate not_2, 16 bits wide
  assign not_3_out = ~Y_2;  // NOT_Gate not_3, 16 bits wide
  assign not_4_out = ~Z_2;  // NOT_Gate not_4, 16 bits wide
  assign w_prime_x_prime_y_prime_z_2_out = not_1_out & not_2_out & not_3_out & Z_2;  // AND_Gate w_prime_x_prime_y_prime_z_2, 16 bits wide
  assign w_prime_x_prime_yz_prime_2_out = not_1_out & not_2_out & Y_2 & not_4_out;  // AND_Gate w_prime_x_prime_yz_prime_2, 16 bits wide
  assign w_prime_xy_prime_z_prime_2_out = not_1_out & X_2 & not_3_out & not_4_out;  // AND_Gate w_prime_xy_prime_z_prime_2, 16 bits wide
  assign w_prime_xyz_2_out = not_1_out & X_2 & Y_2 & Z_2;  // AND_Gate w_prime_xyz_2, 16 bits wide
  assign wxy_prime_z_2_out = W_2 & X_2 & not_3_out & Z_2;  // AND_Gate wxy_prime_z_2, 16 bits wide
  assign wxyz_prime_2_out = W_2 & X_2 & Y_2 & not_4_out;  // AND_Gate wxyz_prime_2, 16 bits wide
  assign wx_prime_y_prime_z_prime_2_out = W_2 & not_2_out & not_3_out & not_4_out;  // AND_Gate wx_prime_y_prime_z_prime_2, 16 bits wide
  assign wx_prime_yz_2_out = W_2 & not_2_out & Y_2 & Z_2;  // AND_Gate wx_prime_yz_2, 16 bits wide
  assign or_1_out = w_prime_x_prime_y_prime_z_2_out | w_prime_x_prime_yz_prime_2_out | w_prime_xy_prime_z_prime_2_out | w_prime_xyz_2_out;  // OR_Gate or_1, 16 bits wide
  assign or_2_out = wxy_prime_z_2_out | wxyz_prime_2_out | wx_prime_y_prime_z_prime_2_out | wx_prime_yz_2_out;  // OR_Gate or_2, 16 bits wide
  assign out_10 = or_1_out | or_2_out;  // OR_Gate or_3, 16 bits wide

  // Notes on the sheet:
  //   Brandon Perez - Lab 3 Part 2
  //   Universal NAND Solution
  //   AND / OR / NOT Gates Solution
endmodule
