// Logisim project Lab3Part3.circ as structural Verilog: 1 circuit, main circuit main
module main (
  input  W,
  input  X,
  input  Y,
  input  Z
);

  wire not_1_out, not_2_out, not_3_out, not_4_out, or_1_out, or_2_out, or_3_out, or_4_out,
       w_prime_x_prime_out, w_prime_y_prime_out, w_prime_z_2_out, w_prime_z_3_out, w_prime_z_out, w_x_y_out,
       x_prime_y_prime_out, x_prime_y_prime_z_prime_out, x_prime_z_out, y_prime_z_prime_2_out,
       y_prime_z_prime_3_out, y_prime_z_prime_out, yz_out;

  not not_1 (not_1_out, W);
  not not_2 (not_2_out, Y);
  not not_3 (not_3_out, X);
  not not_4 (not_4_out, Z);
  and w_prime_x_prime (w_prime_x_prime_out, not_1_out, not_3_out);
  and y_prime_z_prime (y_prime_z_prime_out, not_2_out, not_4_out);
  and w_prime_z (w_prime_z_out, not_1_out, Z);
  or w_x_y (w_x_y_out, W, X, Y);
  or x_prime_y_prime_z_prime (x_prime_y_prime_z_prime_out, not_3_out, not_2_out, not_4_out);
  and w_prime_z_2 (w_prime_z_2_out, not_1_out, Z);
  and y_prime_z_prime_2 (y_prime_z_prime_2_out, not_2_out, not_4_out);
  and w_prime_z_3 (w_prime_z_3_out, not_1_out, Z);
  and w_prime_y_prime (w_prime_y_prime_out, not_1_out, not_2_out);
  and x_prime_z (x_prime_z_out, not_3_out, Z);
  and x_prime_y_prime (x_prime_y_prime_out, not_3_out, not_2_out);
  and y_prime_z_prime_3 (y_prime_z_prime_3_out, not_2_out, not_4_out);
  and yz (yz_out, Y, Z);
  or or_1 (or_1_out, w_prime_x_prime_out, y_prime_z_prime_out, w_prime_z_out);
  or or_2 (or_2_out, w_prime_z_2_out, y_prime_z_prime_2_out);
  or or_3 (or_3_out, w_prime_y_prime_out, x_prime_z_out);
  or or_4 (or_4_out, x_prime_y_prime_out, y_prime_z_prime_3_out, yz_out);
  _7_Segment_Display u_7_segment_display_1 (
    .g(or_4_out), .f(or_3_out), .a(or_1_out), .b(w_x_y_out), .e(w_prime_z_3_out), .d(or_2_out),
    .c(x_prime_y_prime_z_prime_out));  // open: dp

  // Notes on the sheet:
  //   Brandon Perez - Lab 3 Part 3
  //   Logic for Ouput A
  //   Logic for Ouput B
  //   Logic for Ouput C
  //   Logic for Ouput D
  //   Logic for Ouput E
  //   Logic for Ouput F
  //   Logic for Ouput G
endmodule
