// Logisim project Lab3Part4.circ as structural Verilog: 1 circuit, main circuit main
module main (
  input  W,
  input  X,
  input  Y,
  input  Z
);

  wire not_1_out, not_2_out, not_3_out, not_4_out, or_2_out, or_3_out, or_4_out, or_5_out, or_6_out,
       or_7_out, or_out, w_prime_x_out, w_prime_x_prime_2_out, w_prime_x_prime_out, w_prime_y_out,
       w_prime_y_prime_2_out, w_prime_y_prime_out, w_prime_z_2_out, w_prime_z_out, w_prime_z_prime_out,
       wx_2_out, wx_3_out, wx_out, wx_prime_y_prime_out, wy_2_out, wy_3_out, wy_4_out, wy_out,
       x_prime_y_prime_2_out, x_prime_y_prime_out, x_prime_z_out, xz_out, y_prime_z_prime_2_out,
       y_prime_z_prime_3_out, y_prime_z_prime_out, yz_out;

  not not_1 (not_1_out, W);
  not not_2 (not_2_out, X);
  not not_3 (not_3_out, Y);
  not not_4 (not_4_out, Z);
  and w_prime_x_prime (w_prime_x_prime_out, not_1_out, not_2_out);
  and y_prime_z_prime (y_prime_z_prime_out, not_3_out, not_4_out);
  and wy (wy_out, W, Y);
  and xz (xz_out, X, Z);
  and w_prime_x (w_prime_x_out, not_1_out, X);
  and wx_prime_y_prime (wx_prime_y_prime_out, W, not_2_out, not_3_out);
  and w_prime_y (w_prime_y_out, not_1_out, Y);
  and w_prime_x_prime_2 (w_prime_x_prime_2_out, not_1_out, not_2_out);
  and w_prime_z_prime (w_prime_z_prime_out, not_1_out, not_4_out);
  and w_prime_y_prime (w_prime_y_prime_out, not_1_out, not_1_out, not_3_out);
  and x_prime_y_prime (x_prime_y_prime_out, not_2_out, not_3_out);
  and wx (wx_out, W, X);
  and wy_2 (wy_2_out, W, Y);
  and w_prime_z (w_prime_z_out, not_1_out, not_1_out, Z);
  and y_prime_z_prime_2 (y_prime_z_prime_2_out, not_3_out, not_4_out);
  and wx_2 (wx_2_out, W, X);
  and wy_3 (wy_3_out, W, Y);
  and w_prime_z_2 (w_prime_z_2_out, not_1_out, not_1_out, Z);
  and wx_3 (wx_3_out, W, X);
  and wy_4 (wy_4_out, W, Y);
  and w_prime_y_prime_2 (w_prime_y_prime_2_out, not_1_out, not_1_out, not_3_out);
  and x_prime_z (x_prime_z_out, not_2_out, Z);
  and x_prime_y_prime_2 (x_prime_y_prime_2_out, not_2_out, not_3_out);
  and y_prime_z_prime_3 (y_prime_z_prime_3_out, not_3_out, not_3_out, not_4_out);
  and yz (yz_out, Y, Z);
  or \or  (or_out, w_prime_x_prime_out, y_prime_z_prime_out, wy_out, xz_out);
  or or_2 (or_2_out, w_prime_x_out, wx_prime_y_prime_out, w_prime_y_out);
  or or_3 (or_3_out, w_prime_x_prime_2_out, w_prime_z_prime_out, w_prime_y_prime_out, x_prime_y_prime_out);
  or or_4 (or_4_out, wx_out, wy_2_out, w_prime_z_out, y_prime_z_prime_2_out);
  or or_5 (or_5_out, wx_2_out, wy_3_out, w_prime_z_2_out);
  or or_6 (or_6_out, wx_3_out, wy_4_out, w_prime_y_prime_2_out, x_prime_z_out);
  or or_7 (or_7_out, x_prime_y_prime_2_out, W, y_prime_z_prime_3_out, yz_out);
  _7_Segment_Display u_7_segment_display_1 (
    .g(or_7_out), .f(or_6_out), .a(or_out), .b(or_2_out), .e(or_5_out), .d(or_4_out), .c(or_3_out));  // open: dp

  // Notes on the sheet:
  //   Brandon Perez - Lab 3 Part 4
  //   Logic for Ouput A
  //   Logic for Ouput B
  //   Logic for Ouput C
  //   Logic for Ouput D
  //   Logic for Ouput E
  //   Logic for Ouput F
  //   Logic for Ouput G
endmodule
