// Logisim project Lab4.Part2.circ as structural Verilog: 1 circuit, main circuit main
module main (
  input  y,
  input  z,
  input  [15:0] in_3,
  input  [1:0] w_x,
  input  in_5,
  output out_6
);

  wire and_1_out, and_2_out, and_3_out, and_4_out, not_1_out, not_2_out, not_3_out, or_1_out;

  not not_1 (not_1_out, y);
  not not_2 (not_2_out, z);
  and and_1 (and_1_out, z, not_1_out);
  and and_2 (and_2_out, y, not_2_out);
  and and_3 (and_3_out, y, z);
  and and_4 (and_4_out, not_2_out, not_1_out);
  not not_3 (not_3_out, and_2_out);
  or or_1 (or_1_out, and_3_out, and_4_out);
  Multiplexer #(.select(2)) multiplexer_1 (
    .in0(and_1_out), .in1(not_3_out), .in2(or_1_out), .in3(y), .out(out_6), .sel(w_x), .en(in_5));

  // Notes on the sheet:
  //   Brandon Perez - Lab 4 Part 2
  //   desired output
endmodule
