// Logisim project Lab4Part1.circ as structural Verilog
module Half_Adder (
  input  x,
  input  y,
  output Sum,
  output Carry
);

  xor xor_1 (Sum, x, y);
  and and_1 (Carry, x, y);

  // Notes on the sheet:
  //   Truth Table
  //   x | y | sum | carry
  //   0 | 0 |  0  |  0
  //   0 | 1 |  1  |  0
  //   1 | 0 |  1  |  0
  //   1 | 1 |  0  |  1
  //   Half Adder
endmodule

module Full_Adder (
  input  x,
  input  y,
  input  Carry_In,
  output Sum,
  output Carry_Out
);

  wire half_adder_1_carry, half_adder_1_sum, half_adder_2_carry;

  Half_Adder half_adder_1 (.x(x), .y(y), .Sum(half_adder_1_sum), .Carry(half_adder_1_carry));
  Half_Adder half_adder_2 (.x(half_adder_1_sum), .y(Carry_In), .Sum(Sum), .Carry(half_adder_2_carry));
  or or_1 (Carry_Out, half_adder_1_carry, half_adder_2_carry);

  // Notes on the sheet:
  //   Truth Table
  //   x  | y | c-in | sum | c-out
  //   0 | 0 |   0    |   0    |    0    
  //   0 | 0 |   1    |   1    |    0    
  //   0 | 1 |   0    |   1    |    0    
  //   0 | 1 |   1    |   0    |    1    
  //   1 | 0 |   0    |   1    |    0    
  //   1 | 0 |   1    |   0    |    1    
  //   1 | 1 |   0    |   0    |    1    
  //   1 | 1 |   1    |   1    |    1    
  //   Full Adder
endmodule

module main (
  input  [3:0] x,
  input  [3:0] y,
  input  [7:0] x_2,
  input  [7:0] y_2,
  input  [7:0] Carry_In,
  input  x1,
  input  x2,
  input  x3,
  input  y1,
  input  y2,
  input  y3,
  input  carry_in_2,
  output [3:0] Sum,
  output [3:0] Carry,
  output [7:0] out_15,
  output [7:0] out_16,
  output overflow,
  output out_18,
  output out_19,
  output out_20
);

  wire full_adder_2_carry_out, full_adder_3_carry_out;
  wire [7:0] and_2_out, and_3_out, xor_2_out;

  assign Sum = x ^ y;  // XOR_Gate xor_1, 4 bits wide
  assign Carry = x & y;  // AND_Gate and_1, 4 bits wide
  Full_Adder full_adder_1 (.x(x1), .y(y1), .Carry_In(full_adder_2_carry_out), .Sum(out_18), .Carry_Out(overflow));
  Full_Adder full_adder_2 (
    .x(x2), .y(y2), .Carry_In(full_adder_3_carry_out), .Sum(out_19), .Carry_Out(full_adder_2_carry_out));
  Full_Adder full_adder_3 (.x(x3), .y(y3), .Carry_In(carry_in_2), .Sum(out_20), .Carry_Out(full_adder_3_carry_out));
  assign xor_2_out = x_2 ^ y_2;  // XOR_Gate xor_2, 8 bits wide
  assign and_2_out = x_2 & y_2;  // AND_Gate and_2, 8 bits wide
  assign out_15 = xor_2_out ^ Carry_In;  // XOR_Gate xor_3, 8 bits wide
  assign and_3_out = xor_2_out & Carry_In;  // AND_Gate and_3, 8 bits wide
  assign out_16 = and_3_out | and_2_out;  // OR_Gate or_1, 8 bits wide

  // Notes on the sheet:
  //   Truth Table
  //   x | y | sum | carry
  //   0 | 0 |  0  |  0
  //   0 | 1 |  1  |  0
  //   1 | 0 |  1  |  0
  //   1 | 1 |  0  |  1
  //   Truth Table
  //   x | y | c-in | sum | c-out
  //   0 | 0 |   0    |   0    |    0    
  //   0 | 0 |   1    |   1    |    0    
  //   0 | 1 |   0    |   1    |    0    
  //   0 | 1 |   1    |   0    |    1    
  //   1 | 0 |   0    |   1    |    0    
  //   1 | 0 |   1    |   0    |    1    
  //   1 | 1 |   0    |   0    |    1    
  //   1 | 1 |   1    |   1    |    1    
  //   Half Adder
  //   Full Adder
  //   3 Bit Binary Adder
endmodule

module EC (
  input  x5,
  input  x4,
  input  x3,
  input  x2,
  input  x1,
  input  x0,
  input  y5,
  input  y4,
  input  y3,
  input  y2,
  input  y1,
  input  y0,
  input  carry_in,
  output s4,
  output s3,
  output s2,
  output s1,
  output s0,
  output overflow
);

  wire full_adder_1_carry_out, full_adder_2_carry_out, full_adder_3_carry_out, full_adder_4_carry_out,
       xor_1_out, xor_2_out, xor_3_out, xor_4_out, xor_5_out, xor_6_out, xor_7_out, xor_8_out, xor_9_out,
       xor_10_out;

  xor xor_1 (xor_1_out, x5, x4);
  xor xor_2 (xor_2_out, x5, x3);
  xor xor_3 (xor_3_out, x5, x2);
  xor xor_4 (xor_4_out, x0, x5);
  xor xor_5 (xor_5_out, x5, x1);
  Full_Adder full_adder_1 (
    .x(xor_4_out), .y(xor_10_out), .Carry_In(carry_in), .Sum(s0), .Carry_Out(full_adder_1_carry_out));
  Full_Adder full_adder_2 (
    .x(xor_5_out), .y(xor_9_out), .Carry_In(full_adder_1_carry_out), .Sum(s1),
    .Carry_Out(full_adder_2_carry_out));
  Full_Adder full_adder_3 (
    .x(xor_3_out), .y(xor_8_out), .Carry_In(full_adder_2_carry_out), .Sum(s2),
    .Carry_Out(full_adder_3_carry_out));
  Full_Adder full_adder_4 (
    .x(xor_2_out), .y(xor_7_out), .Carry_In(full_adder_3_carry_out), .Sum(s3),
    .Carry_Out(full_adder_4_carry_out));
  Full_Adder full_adder_5 (
    .x(xor_1_out), .y(xor_6_out), .Carry_In(full_adder_4_carry_out), .Sum(s4), .Carry_Out(overflow));
  xor xor_6 (xor_6_out, y5, y4);
  xor xor_7 (xor_7_out, y5, y3);
  xor xor_8 (xor_8_out, y5, y2);
  xor xor_9 (xor_9_out, y5, y1);
  xor xor_10 (xor_10_out, y0, y5);
endmodule
